# Fritzing sketch 400pins (saved by Fritzing 0.9.3b)
breadboards: 1

parts:
  Componente1 = Arduino Uno (Rev3)
  Componente2 = FC-28 Soil Hygrometer Module
  Componente3 = FC-28 Soil Hygrometer Module - Probe
  S1 = Pushbutton [package="[THT]"]
  R1 = Resistor [tolerance=±5% resistance=330 package=THT]
  LED1 = LED - 3mm [color="Red (633nm)" package="3 mm [THT]"]
  LED2 = LED - 3mm [color="Red (633nm)" package="3 mm [THT]"]
  LED3 = LED - 3mm [color="Yellow (592nm)" package="3 mm [THT]"]
  LED4 = LED - 3mm [color="Yellow (592nm)" package="3 mm [THT]"]
  LED5 = LED - 3mm [color="Green (565nm)" package="3 mm [THT]"]
  LED6 = LED - 3mm [color="Green (565nm)" package="3 mm [THT]"]
  R2 = Resistor [tolerance=±5% resistance=330 package=THT]
  R3 = Resistor [tolerance=±5% resistance=330 package=THT]
  R4 = Resistor [tolerance=±5% resistance=330 package=THT]
  R5 = Resistor [tolerance=±5% resistance=330 package=THT]
  R6 = Resistor [tolerance=±5% resistance=330 package=THT]
  R7 = Resistor [tolerance=±5% resistance=10k package=THT]
  M1 = DC Motor

nets:
  N1: Componente1.A1, Componente2.AO
  N2: Componente1.D10_PWM/SS, S1.Pin_3, S1.Pin_4, R7.Pin_1
  N3: Componente1.D12/MISO, M1.pin_2
  GND: Componente1.GND, Componente2.GND, LED1.cathode, LED2.cathode, LED3.cathode, LED4.cathode, LED5.cathode, LED6.cathode, R7.Pin_0, M1.pin_1
  N4: Componente1.D2, R6.Pin_0
  N5: Componente1.D3_PWM, R5.Pin_0
  N6: Componente1.D4, R3.Pin_0
  N7: Componente1.D5_PWM, R4.Pin_0
  N8: Componente1.D6_PWM, R2.Pin_0
  N9: Componente1.D7, R1.Pin_0
  5V: Componente1.5V, Componente2.VCC, S1.Pin_1, S1.Pin_2
  N10: Componente2.POS, Componente3.POS
  N11: Componente2.NEG, Componente3.NEG
  N12: R1.Pin_1, LED1.anode
  N13: LED2.anode, R2.Pin_1
  N14: LED3.anode, R4.Pin_1
  N15: LED4.anode, R3.Pin_1
  N16: LED5.anode, R5.Pin_1
  N17: LED6.anode, R6.Pin_1

custom parts:
  FC-28 Soil Hygrometer Module: The FC-28 is a soil hygrometer module that uses the Texas Instruments LM393 comparator chip to provide an analog measurement of soil humidity. The digital output is high when soil moisture is over a certain threshold, as determined by adjusting the potentiometer.
  FC-28 Soil Hygrometer Module - Probe: The FC-28 is a soil hygrometer module that uses the Texas Instruments LM393 comparator chip to provide an analog measurement of soil humidity.
