# Fritzing sketch 800pins (saved by Fritzing 0.9.3b)
breadboards: 1

parts:
  Componente1 = Arduino Uno (Rev3)
  LED1 = LED - 3mm [color="Red (633nm)" package="3 mm [THT]"]
  LED2 = LED - 3mm [color="Red (633nm)" package="3 mm [THT]"]
  M1 = DC Motor
  R1 = Resistor [tolerance=±5% resistance=330 package=THT]
  LED3 = LED - 3mm [color="Yellow (595nm)" package="3 mm [THT]"]
  R2 = Resistor [tolerance=±5% resistance=330 package=THT]
  R3 = Resistor [tolerance=±5% resistance=330 package=THT]
  LED4 = LED - 3mm [color="Yellow (595nm)" package="3 mm [THT]"]
  R4 = Resistor [tolerance=±5% resistance=330 package=THT]
  LED5 = LED - 3mm [color="Green (555nm)" package="3 mm [THT]"]
  R5 = Resistor [tolerance=±5% resistance=330 package=THT]
  R6 = Resistor [tolerance=±5% resistance=330 package=THT]
  LED6 = LED - 3mm [color="Green (555nm)" package="3 mm [THT]"]
  S1 = Pushbutton [package="[THT]"]
  R7 = Resistor [tolerance=±5% resistance=10k package=THT]
  Componente2 = FC-28 Soil Hygrometer Module
  Componente3 = FC-28 Soil Hygrometer Module - Probe

nets:
  N1: Componente1.A1, Componente2.AO
  N2: Componente1.D10_PWM/SS, S1.Pin_1, S1.Pin_2, R7.Pin_0
  N3: Componente1.D12/MISO, M1.pin_2
  GND: Componente1.GND, LED1.cathode, LED2.cathode, M1.pin_1, LED3.cathode, LED4.cathode, LED5.cathode, LED6.cathode, R7.Pin_1, Componente2.GND
  N4: Componente1.D2, R6.Pin_1
  N5: Componente1.D3_PWM, R5.Pin_1
  N6: Componente1.D4, R4.Pin_1
  N7: Componente1.D5_PWM, R3.Pin_1
  N8: Componente1.D6_PWM, R2.Pin_1
  N9: Componente1.D7, R1.Pin_1
  5V: Componente1.5V, S1.Pin_3, S1.Pin_4, Componente2.VCC
  N10: LED1.anode, R1.Pin_0
  N11: LED2.anode, R2.Pin_0
  N12: LED3.anode, R3.Pin_0
  N13: LED4.anode, R4.Pin_0
  N14: LED5.anode, R5.Pin_0
  N15: R6.Pin_0, LED6.anode
  N16: Componente2.POS, Componente3.POS
  N17: Componente2.NEG, Componente3.NEG

custom parts:
  FC-28 Soil Hygrometer Module: The FC-28 is a soil hygrometer module that uses the Texas Instruments LM393 comparator chip to provide an analog measurement of soil humidity. The digital output is high when soil moisture is over a certain threshold, as determined by adjusting the potentiometer.
  FC-28 Soil Hygrometer Module - Probe: The FC-28 is a soil hygrometer module that uses the Texas Instruments LM393 comparator chip to provide an analog measurement of soil humidity.
